# Fritzing sketch Esquema_piano (saved by Fritzing 0.6.3b)
breadboards: 1

parts:
  Arduino1 = Arduino
  SPKR1 = Loudspeaker
  R1 = Resistor [tolerance=±5% resistance=220 package=THT]
  R2 = Resistor [tolerance=±5% resistance=220 package=THT]
  R3 = Resistor [tolerance=±5% resistance=220 package=THT]
  R4 = Resistor [tolerance=±5% resistance=220 package=THT]
  R5 = Trimmer Potentiometer [maximum_resistance=10kΩ package=THT]
  LED1 = LED - 5mm [color="Red (633nm)" package="5 mm [THT]"]
  S1 = Pushbutton [package="[THT]"]
  R6 = Resistor [tolerance=±5% resistance=220 package=THT]
  R7 = Resistor [tolerance=±5% resistance=220 package=THT]
  R8 = Resistor [tolerance=±5% resistance=220 package=THT]

nets:
  N1: Arduino1.D13, S1.Pin_3, S1.Pin_4
  N2: Arduino1.D11, SPKR1.pin2
  N3: Arduino1.D10, R4.Pin_1
  N4: Arduino1.D9, R8.Pin_1
  N5: Arduino1.D8, R3.Pin_1
  N6: Arduino1.D7, R6.Pin_1
  N7: Arduino1.D6, R2.Pin_1
  N8: Arduino1.D5, R7.Pin_1
  N9: Arduino1.D4, R1.Pin_1
  N10: Arduino1.D2, R1.Pin_0, R2.Pin_0, R3.Pin_0, R4.Pin_0, R6.Pin_0, R7.Pin_0, R8.Pin_0
  N11: Arduino1.+5V, R5.leg2
  N12: Arduino1.GND, SPKR1.pin1, R5.leg1, LED1.cathode, S1.Pin_1, S1.Pin_2
  N13: Arduino1.A0, LED1.anode

notes:
  Aqui van los sensores
